# Fritzing sketch Sketch 8 (saved by Fritzing 0.8.7b)
stripboards: 1

parts:
  Raspberry_Pi_1 = Raspberry Pi 3
  7805 = Voltage Regulator [package=to220-igo]
  12V_POWER_SUPPLY = Header 2 [package=screwterminal-3.5mm-2_lock]
  Keypad = Header 6 [package=1x06_smd_straight_alt]
  Enviro_Hat = Header 6 [package=1x06_smd_straight_alt]
  GerBot = Header 6 [package=1x06_smd_straight_alt]
  FAN = Header 2 [package=screwterminal-3.5mm-2_lock]  # not connected
  CONDENSER = Header 2 [package=screwterminal-3.5mm-2_lock]  # not connected
  LED1 = Header 2 [package=screwterminal-3.5mm-2_lock]
  LED2 = Header 2 [package=screwterminal-3.5mm-2_lock]
  EV = Header 2 [package=screwterminal-3.5mm-2_lock]
  MAIN_SWITCH = SWITCH-SPST-2 [package=switch-spst-vertical]
  Automation_Hat = Header 8 [package=1x08_smd_alt]

nets:
  N1: Raspberry_Pi_1.GPIO2, Enviro_Hat.3
  N2: Raspberry_Pi_1.GPIO3, Enviro_Hat.2
  N3: Raspberry_Pi_1.GIPO4, Enviro_Hat.1
  N4: Raspberry_Pi_1.GIPO10, Automation_Hat.5
  N5: Raspberry_Pi_1.GIPO9, Automation_Hat.1
  N6: Raspberry_Pi_1.GIPO11, Automation_Hat.4
  N7: Raspberry_Pi_1.GIPO26, Keypad.4
  N8: Raspberry_Pi_1.GIPO21, Keypad.1
  N9: Raspberry_Pi_1.GIPO20, Keypad.2
  N10: Raspberry_Pi_1.GIPO16, Keypad.3
  N11: Raspberry_Pi_1.GIPO7, Automation_Hat.2
  N12: Raspberry_Pi_1.GIPO25, Automation_Hat.3
  N13: Raspberry_Pi_1.GIPO15, GerBot.6
  N14: Raspberry_Pi_1.GIPO14, GerBot.5
  N15: 7805.GND, EV.1, MAIN_SWITCH.P
  N16: 7805.IN, 7805.OUT, 12V_POWER_SUPPLY.2, LED1.1, LED1.2, LED2.1, LED2.2
  N17: 12V_POWER_SUPPLY.1, MAIN_SWITCH.O
  N18: GerBot.2, EV.2

notes:
  OD0
  SPI-CLK
  BLIGHT
  SPI-MOSI
  LEFT
  UP
  DOWN
  UART-TX
  SDA
  SCL
  SCL-INT
  UART-RX
  RIGHT
